// Logisim project 4_16decoder.circ as structural Verilog: 2 circuits, main circuit binarydecoder
module binarydecoder (
  input  lsb,
  input  msb,
  input  en,
  output out_4,
  output out_5,
  output out_6,
  output out_7
);

  and and_1 (out_4, ~lsb, ~msb, en);  // AND_Gate
  and and_2 (out_5, lsb, ~msb, en);  // AND_Gate
  and and_3 (out_6, ~lsb, en, msb);  // AND_Gate
  and and_4 (out_7, lsb, en, msb);
endmodule

module biggerdecoder (
  input  lsb,
  input  in_2,
  input  in_3,
  input  msb,
  input  in_5
);

  wire binarydecoder_1_out_4, binarydecoder_1_out_5, binarydecoder_1_out_6, binarydecoder_1_out_7,
       binarydecoder_2_out_4, binarydecoder_2_out_5, binarydecoder_2_out_6, binarydecoder_2_out_7,
       binarydecoder_3_out_4, binarydecoder_3_out_6, binarydecoder_3_out_7, binarydecoder_4_out_4,
       binarydecoder_4_out_5, binarydecoder_4_out_6, binarydecoder_4_out_7, binarydecoder_5_out_4,
       binarydecoder_5_out_5, binarydecoder_5_out_6, binarydecoder_5_out_7;

  binarydecoder binarydecoder_1 (
    .lsb(in_3), .msb(msb), .en(in_5), .out_4(binarydecoder_1_out_4), .out_5(binarydecoder_1_out_5),
    .out_6(binarydecoder_1_out_6), .out_7(binarydecoder_1_out_7));
  binarydecoder binarydecoder_2 (
    .lsb(lsb), .msb(in_2), .en(binarydecoder_1_out_4), .out_4(binarydecoder_2_out_4),
    .out_5(binarydecoder_2_out_5), .out_6(binarydecoder_2_out_6), .out_7(binarydecoder_2_out_7));
  binarydecoder binarydecoder_3 (
    .lsb(lsb), .msb(in_2), .en(binarydecoder_1_out_5), .out_4(binarydecoder_3_out_4),
    .out_5(binarydecoder_3_out_4), .out_6(binarydecoder_3_out_6), .out_7(binarydecoder_3_out_7));
  binarydecoder binarydecoder_4 (
    .lsb(lsb), .msb(in_2), .en(binarydecoder_1_out_6), .out_4(binarydecoder_4_out_4),
    .out_5(binarydecoder_4_out_5), .out_6(binarydecoder_4_out_6), .out_7(binarydecoder_4_out_7));
  binarydecoder binarydecoder_5 (
    .lsb(lsb), .msb(in_2), .en(binarydecoder_1_out_7), .out_4(binarydecoder_5_out_4),
    .out_5(binarydecoder_5_out_5), .out_6(binarydecoder_5_out_6), .out_7(binarydecoder_5_out_7));
endmodule
