// Logisim project 8_bit_ALU.circ as structural Verilog: 3 circuits, main circuit 8BitALU
module _8BitALU (
  input  LSR,
  input  LSL,
  input  XOR,
  input  OR,
  input  AND,
  input  addSub,
  input  sub,
  input  [7:0] secondbyte,
  input  [7:0] fistbyte,
  output [7:0] out_10,
  output cout
);

  wire [7:0] adder_1_out, and_1_out, bit_extender_1_out, leftshift_1_out_2, or_1_out, rightshift_1_out_2,
       xor_1_out, xor_2_out;

  assign bit_extender_1_out = {{7{sub}}, sub};  // Bit_Extender bit_extender_1
  assign xor_1_out = bit_extender_1_out ^ secondbyte;  // XOR_Gate xor_1, 8 bits wide
  assign and_1_out = secondbyte & fistbyte;  // AND_Gate and_1, 8 bits wide
  assign or_1_out = secondbyte | fistbyte;  // OR_Gate or_1, 8 bits wide
  assign xor_2_out = secondbyte ^ fistbyte;  // XOR_Gate xor_2, 8 bits wide
  LeftShift leftshift_1 (.in_1(fistbyte), .out_2(leftshift_1_out_2));
  rightShift rightshift_1 (.in_1(fistbyte), .out_2(rightshift_1_out_2));
  Adder adder_1 (.a(xor_1_out), .b(fistbyte), .out(adder_1_out), .cin(sub), .cout(cout));
  assign out_10 = addSub ? adder_1_out : 8'bz;  // Controlled_Buffer controlled_buffer_1
  assign out_10 = AND ? and_1_out : 8'bz;  // Controlled_Buffer controlled_buffer_2
  assign out_10 = OR ? or_1_out : 8'bz;  // Controlled_Buffer controlled_buffer_3
  assign out_10 = XOR ? xor_2_out : 8'bz;  // Controlled_Buffer controlled_buffer_4
  assign out_10 = LSL ? leftshift_1_out_2 : 8'bz;  // Controlled_Buffer controlled_buffer_5
  assign out_10 = LSR ? rightshift_1_out_2 : 8'bz;  // Controlled_Buffer controlled_buffer_6
endmodule

module LeftShift (
  input  [7:0] in_1,
  output [7:0] out_2
);


  assign out_2 = {in_1[6:0], 1'b0};
endmodule

module rightShift (
  input  [7:0] in_1,
  output [7:0] out_2
);


  assign out_2 = {1'b0, in_1[7:1]};
endmodule
