// Logisim project 8_bit_RAM.circ as structural Verilog: 1 circuit, main circuit main
module main (
  input  in_1,
  input  [2:0] in_2,
  input  [7:0] in_3,
  input  in_4,
  input  in_5,
  output [7:0] out_6
);

  wire and_1_out, and_2_out, and_3_out, and_4_out, and_5_out, and_6_out, and_7_out, and_8_out, and_9_out,
       and_10_out, and_11_out, and_12_out, and_13_out, and_14_out, and_15_out, and_16_out, clk_out,
       decoder_1_out0, decoder_1_out1, decoder_1_out2, decoder_1_out3, decoder_1_out4, decoder_1_out5,
       decoder_1_out6, decoder_1_out7;
  wire [7:0] register_1_q, register_2_q, register_3_q, register_4_q, register_5_q, register_6_q,
       register_7_q, register_8_q;

  Decoder #(.select(3)) decoder_1 (
    .out0(decoder_1_out0), .out1(decoder_1_out1), .out2(decoder_1_out2), .out3(decoder_1_out3),
    .out4(decoder_1_out4), .out5(decoder_1_out5), .out6(decoder_1_out6), .out7(decoder_1_out7), .sel(in_2),
    .en(in_1));
  Clock clk (.out(clk_out));
  and and_1 (and_1_out, ~in_4, decoder_1_out0);  // AND_Gate
  and and_2 (and_2_out, decoder_1_out0, in_4);
  and and_3 (and_3_out, ~in_4, decoder_1_out1);  // AND_Gate
  and and_4 (and_4_out, decoder_1_out1, in_4);
  and and_5 (and_5_out, ~in_4, decoder_1_out2);  // AND_Gate
  and and_6 (and_6_out, decoder_1_out2, in_4);
  and and_7 (and_7_out, ~in_4, decoder_1_out3);  // AND_Gate
  and and_8 (and_8_out, decoder_1_out3, in_4);
  and and_9 (and_9_out, ~in_4, decoder_1_out4);  // AND_Gate
  and and_10 (and_10_out, decoder_1_out4, in_4);
  and and_11 (and_11_out, ~in_4, decoder_1_out5);  // AND_Gate
  and and_12 (and_12_out, decoder_1_out5, in_4);
  and and_13 (and_13_out, ~in_4, decoder_1_out6);  // AND_Gate
  and and_14 (and_14_out, decoder_1_out6, in_4);
  and and_15 (and_15_out, ~in_4, decoder_1_out7);  // AND_Gate
  and and_16 (and_16_out, decoder_1_out7, in_4);
  Register register_1 (.D(out_6), .en(and_1_out), .Q(register_1_q), .clk(clk_out));  // open: clr
  Register register_2 (.D(out_6), .en(and_3_out), .Q(register_2_q), .clk(clk_out));  // open: clr
  Register register_3 (.D(out_6), .en(and_5_out), .Q(register_3_q), .clk(clk_out));  // open: clr
  Register register_4 (.D(out_6), .en(and_7_out), .Q(register_4_q), .clk(clk_out));  // open: clr
  Register register_5 (.D(out_6), .en(and_9_out), .Q(register_5_q), .clk(clk_out));  // open: clr
  Register register_6 (.D(out_6), .en(and_11_out), .Q(register_6_q), .clk(clk_out));  // open: clr
  Register register_7 (.D(out_6), .en(and_13_out), .Q(register_7_q), .clk(clk_out));  // open: clr
  Register register_8 (.D(out_6), .en(and_15_out), .Q(register_8_q), .clk(clk_out));  // open: clr
  assign out_6 = and_2_out ? register_1_q : 8'bz;  // Controlled_Buffer controlled_buffer_1
  assign out_6 = and_4_out ? register_2_q : 8'bz;  // Controlled_Buffer controlled_buffer_2
  assign out_6 = and_6_out ? register_3_q : 8'bz;  // Controlled_Buffer controlled_buffer_3
  assign out_6 = and_8_out ? register_4_q : 8'bz;  // Controlled_Buffer controlled_buffer_4
  assign out_6 = and_10_out ? register_5_q : 8'bz;  // Controlled_Buffer controlled_buffer_5
  assign out_6 = and_12_out ? register_6_q : 8'bz;  // Controlled_Buffer controlled_buffer_6
  assign out_6 = and_14_out ? register_7_q : 8'bz;  // Controlled_Buffer controlled_buffer_7
  assign out_6 = and_16_out ? register_8_q : 8'bz;  // Controlled_Buffer controlled_buffer_8
  assign out_6 = in_5 ? in_3 : 8'bz;  // Controlled_Buffer controlled_buffer_9

  // Notes on the sheet:
  //   read/nwrite
endmodule
