// Logisim project processor1.circ as structural Verilog: 14 circuits, main circuit fulladder
module fulladder (
  input  a,
  input  b,
  input  c,
  output x,
  output y
);

  wire nand_1_out, nand_2_out, nand_3_out, nand_4_out, nand_5_out, nand_6_out, nand_7_out, nand_8_out,
       nand_9_out, nand_11_out, nand_12_out, nand_13_out, nand_14_out;

  nand nand_1 (nand_1_out, b, c);
  nand nand_2 (nand_2_out, a, c);
  nand nand_3 (nand_3_out, a, b);
  nand nand_4 (nand_4_out, a, a);
  nand nand_5 (nand_5_out, b, b);
  nand nand_6 (nand_6_out, a, a);
  nand nand_7 (nand_7_out, c, c);
  nand nand_8 (nand_8_out, b, b);
  nand nand_9 (nand_9_out, c, c);
  nand nand_10 (x, nand_1_out, nand_2_out, nand_3_out);
  nand nand_11 (nand_11_out, nand_4_out, nand_5_out, c);
  nand nand_12 (nand_12_out, nand_6_out, b, nand_7_out);
  nand nand_13 (nand_13_out, a, nand_8_out, nand_9_out);
  nand nand_14 (nand_14_out, a, b, c);
  nand nand_15 (y, nand_11_out, nand_12_out, nand_13_out, nand_14_out);
endmodule

module add4 (
  input  [3:0] in_1,
  input  [3:0] in_2,
  input  in_3,
  output out_4,
  output [3:0] out_5
);

  wire fulladder_2_x, fulladder_3_x, fulladder_4_x;

  fulladder fulladder_1 (.a(in_1[3]), .b(in_2[3]), .c(fulladder_2_x), .x(out_4), .y(out_5[3]));
  fulladder fulladder_2 (.a(in_1[2]), .b(in_2[2]), .c(fulladder_3_x), .x(fulladder_2_x), .y(out_5[2]));
  fulladder fulladder_3 (.a(in_1[1]), .b(in_2[1]), .c(fulladder_4_x), .x(fulladder_3_x), .y(out_5[1]));
  fulladder fulladder_4 (.a(in_1[0]), .b(in_2[0]), .c(in_3), .x(fulladder_4_x), .y(out_5[0]));
endmodule

module ALU8 (
  input  LSR,
  input  LSL,
  input  XOR,
  input  OR,
  input  AND,
  input  add,
  input  sub,
  input  [7:0] secondbyte,
  input  [7:0] fistbyte,
  output [7:0] out_10,
  output cout,
  output Z,
  output s
);

  wire adder_1_cout, leftshift_1_out_3, or_2_out, rightshift_1_out_2;
  wire [7:0] adder_1_out, and_1_out, bit_extender_1_out, leftshift_1_out_2, or_1_out, rightshift_1_out_3,
       xor_1_out, xor_2_out;

  assign bit_extender_1_out = {{7{sub}}, sub};  // Bit_Extender bit_extender_1
  assign xor_1_out = bit_extender_1_out ^ secondbyte;  // XOR_Gate xor_1, 8 bits wide
  assign and_1_out = secondbyte & fistbyte;  // AND_Gate and_1, 8 bits wide
  assign or_1_out = secondbyte | fistbyte;  // OR_Gate or_1, 8 bits wide
  assign xor_2_out = secondbyte ^ fistbyte;  // XOR_Gate xor_2, 8 bits wide
  leftshift leftshift_1 (.in_1(fistbyte), .out_2(leftshift_1_out_2), .out_3(leftshift_1_out_3));
  rightshift rightshift_1 (.in_1(fistbyte), .out_3(rightshift_1_out_3), .out_2(rightshift_1_out_2));
  Adder adder_1 (.a(xor_1_out), .b(fistbyte), .out(adder_1_out), .cin(sub), .cout(adder_1_cout));
  or or_2 (or_2_out, add, sub);
  assign cout = LSL ? leftshift_1_out_3 : 1'bz;  // Controlled_Buffer controlled_buffer_1
  assign cout = or_2_out ? adder_1_cout : 1'bz;  // Controlled_Buffer controlled_buffer_2
  assign cout = LSR ? rightshift_1_out_2 : 1'bz;  // Controlled_Buffer controlled_buffer_3
  assign out_10 = or_2_out ? adder_1_out : 8'bz;  // Controlled_Buffer controlled_buffer_4
  assign out_10 = AND ? and_1_out : 8'bz;  // Controlled_Buffer controlled_buffer_5
  assign out_10 = OR ? or_1_out : 8'bz;  // Controlled_Buffer controlled_buffer_6
  assign out_10 = XOR ? xor_2_out : 8'bz;  // Controlled_Buffer controlled_buffer_7
  assign out_10 = LSL ? leftshift_1_out_2 : 8'bz;  // Controlled_Buffer controlled_buffer_8
  assign out_10 = LSR ? rightshift_1_out_3 : 8'bz;  // Controlled_Buffer controlled_buffer_9
  nor nor_1 (Z, out_10[0], out_10[1], out_10[2], out_10[3], out_10[5], out_10[6], out_10[7], out_10[4]);

  assign s = out_10[7];

  // Notes on the sheet:
  //   Flag generation circuit
endmodule

module leftshift (
  input  [7:0] in_1,
  output [7:0] out_2,
  output out_3
);


  assign out_2 = {in_1[6:0], 1'b0};
  assign out_3 = in_1[7];
endmodule

module rightshift (
  input  [7:0] in_1,
  output out_2,
  output [7:0] out_3
);


  assign out_2 = in_1[0];
  assign out_3 = {1'b0, in_1[7:1]};
endmodule

module cpu (
  input  clr,
  input  [20:0] con_alu
);

  wire alu8_1_cout, alu8_1_s, alu8_1_z, clock_1_out, decoder_1_out0, decoder_1_out1, decoder_1_out2,
       decoder_1_out3, decoder_1_out4, decoder_1_out5, decoder_1_out6;
  wire [2:0] d_ff_1_q;
  wire [7:0] alu8_1_out_10, controlled_buffer_1_out, counter_1_q, multiplexer_1_out, multiplexer_2_out,
       multiplexer_3_out, register_1_q, register_2_q;

  Clock clock_1 (.out(clock_1_out));
  Register register_1 (.D(alu8_1_out_10), .en(con_alu[0]), .Q(register_1_q), .clk(clock_1_out), .clr(clr));
  Register register_2 (.D(alu8_1_out_10), .en(con_alu[1]), .Q(register_2_q), .clk(clock_1_out), .clr(clr));
  Multiplexer #(.select(3), .width(8), .enable("false")) multiplexer_1 (
    .in0(register_1_q), .in1(register_2_q), .in2(controlled_buffer_1_out), .out(multiplexer_1_out),
    .sel(con_alu[7:5]));  // open: in3, in4, in5, in6, in7
  Multiplexer #(.select(3), .width(8), .enable("false")) multiplexer_2 (
    .in0(register_1_q), .in1(register_2_q), .in2({8{1'b0}}), .out(multiplexer_2_out), .sel(con_alu[4:2]));  // open: in3, in4, in5, in6, in7
  Decoder #(.select(3), .enable("false")) decoder_1 (
    .out0(decoder_1_out0), .out1(decoder_1_out1), .out2(decoder_1_out2), .out3(decoder_1_out3),
    .out4(decoder_1_out4), .out5(decoder_1_out5), .out6(decoder_1_out6), .sel(con_alu[10:8]));  // open: out7
  Counter counter_1 (
    .load(con_alu[15]), .D(alu8_1_out_10), .count(con_alu[16]), .Q(counter_1_q), .clk(clock_1_out), .clr(clr));  // open: carry
  ALU8 alu8_1 (
    .LSR(decoder_1_out6), .LSL(decoder_1_out5), .XOR(decoder_1_out4), .OR(decoder_1_out3),
    .AND(decoder_1_out2), .add(decoder_1_out1), .secondbyte(multiplexer_2_out), .fistbyte(multiplexer_1_out),
    .out_10(alu8_1_out_10), .cout(alu8_1_cout), .sub(decoder_1_out0), .Z(alu8_1_z), .s(alu8_1_s));
  D_Flip_Flop d_ff_1 (
    .clk(clock_1_out), .D(alu8_1_z), .Q(d_ff_1_q[0]), .en(con_alu[13]), .reset(clr));  // open: Qn, preset
  D_Flip_Flop d_ff_2 (
    .clk(clock_1_out), .D(alu8_1_cout), .Q(d_ff_1_q[1]), .en(con_alu[12]), .reset(clr));  // open: Qn, preset
  Multiplexer #(.select(3), .width(8), .enable("false")) multiplexer_3 (
    .in0(multiplexer_1_out), .in1(multiplexer_2_out), .in2(counter_1_q), .out(multiplexer_3_out),
    .sel(con_alu[19:17]));  // open: in3, in4, in5, in6, in7
  D_Flip_Flop d_ff_3 (
    .clk(clock_1_out), .D(alu8_1_s), .Q(d_ff_1_q[2]), .en(con_alu[11]), .reset(clr));  // open: Qn, preset
  assign controlled_buffer_1_out = con_alu[14] ? alu8_1_out_10 : 8'bz;  // Controlled_Buffer controlled_buffer_1
  RAM_part ram_1 (
    .addr(multiplexer_3_out), .data(controlled_buffer_1_out), .sel(1'b1), .clk(clock_1_out), .ld(con_alu[20]));  // open: clr

  // Notes on the sheet:
  //   A
  //   B
  //   Sel-y
  //   Sel-x
  //   F-bus
  //   opperation
  //   IP
  //   A-bus
  //   ALU-o/p
  //   D-bus
endmodule

module latch1 (
  input  D,
  input  en,
  input  in_3,
  output Q
);

  wire and_1_out, and_2_out, nor_1_out, not_1_out, or_1_out;

  not not_1 (not_1_out, D);
  and and_1 (and_1_out, D, en);
  and and_2 (and_2_out, en, not_1_out);
  or or_1 (or_1_out, and_2_out, in_3);
  nor nor_1 (nor_1_out, and_1_out, Q);
  nor nor_2 (Q, nor_1_out, or_1_out);
endmodule

module msDff (
  input  data,
  input  clk,
  input  reset,
  output out_4
);

  wire latch1_1_q, not_1_out;

  latch1 latch1_1 (.D(data), .en(clk), .Q(latch1_1_q), .in_3(reset));
  not not_1 (not_1_out, clk);
  latch1 latch1_2 (.D(latch1_1_q), .en(not_1_out), .Q(out_4), .in_3(reset));
endmodule

module RAM (
  input  in_1,
  input  [2:0] in_2,
  input  [7:0] in_3,
  input  in_4,
  input  in_5,
  input  in_6,
  output [7:0] out_7
);

  wire and_1_out, and_2_out, and_3_out, and_4_out, and_5_out, and_6_out, and_7_out, and_8_out, and_9_out,
       and_10_out, and_11_out, and_12_out, and_13_out, and_14_out, and_15_out, and_16_out, decoder_1_out0,
       decoder_1_out1, decoder_1_out2, decoder_1_out3, decoder_1_out4, decoder_1_out5, decoder_1_out6,
       decoder_1_out7;
  wire [7:0] register_1_q, register_2_q, register_3_q, register_4_q, register_5_q, register_6_q,
       register_7_q, register_8_q;

  Decoder #(.select(3)) decoder_1 (
    .out0(decoder_1_out0), .out1(decoder_1_out1), .out2(decoder_1_out2), .out3(decoder_1_out3),
    .out4(decoder_1_out4), .out5(decoder_1_out5), .out6(decoder_1_out6), .out7(decoder_1_out7), .sel(in_2),
    .en(in_1));
  and and_1 (and_1_out, ~in_4, decoder_1_out0);  // AND_Gate
  and and_2 (and_2_out, decoder_1_out0, in_4);
  and and_3 (and_3_out, ~in_4, decoder_1_out1);  // AND_Gate
  and and_4 (and_4_out, decoder_1_out1, in_4);
  and and_5 (and_5_out, ~in_4, decoder_1_out2);  // AND_Gate
  and and_6 (and_6_out, decoder_1_out2, in_4);
  and and_7 (and_7_out, ~in_4, decoder_1_out3);  // AND_Gate
  and and_8 (and_8_out, decoder_1_out3, in_4);
  and and_9 (and_9_out, ~in_4, decoder_1_out4);  // AND_Gate
  and and_10 (and_10_out, decoder_1_out4, in_4);
  and and_11 (and_11_out, ~in_4, decoder_1_out5);  // AND_Gate
  and and_12 (and_12_out, decoder_1_out5, in_4);
  and and_13 (and_13_out, ~in_4, decoder_1_out6);  // AND_Gate
  and and_14 (and_14_out, decoder_1_out6, in_4);
  and and_15 (and_15_out, ~in_4, decoder_1_out7);  // AND_Gate
  and and_16 (and_16_out, decoder_1_out7, in_4);
  Register register_1 (.D(out_7), .en(and_1_out), .Q(register_1_q), .clk(in_5));  // open: clr
  Register register_2 (.D(out_7), .en(and_3_out), .Q(register_2_q), .clk(in_5));  // open: clr
  Register register_3 (.D(out_7), .en(and_5_out), .Q(register_3_q), .clk(in_5));  // open: clr
  Register register_4 (.D(out_7), .en(and_7_out), .Q(register_4_q), .clk(in_5));  // open: clr
  Register register_5 (.D(out_7), .en(and_9_out), .Q(register_5_q), .clk(in_5));  // open: clr
  Register register_6 (.D(out_7), .en(and_11_out), .Q(register_6_q), .clk(in_5));  // open: clr
  Register register_7 (.D(out_7), .en(and_13_out), .Q(register_7_q), .clk(in_5));  // open: clr
  Register register_8 (.D(out_7), .en(and_15_out), .Q(register_8_q), .clk(in_5));  // open: clr
  assign out_7 = and_2_out ? register_1_q : 8'bz;  // Controlled_Buffer controlled_buffer_1
  assign out_7 = and_4_out ? register_2_q : 8'bz;  // Controlled_Buffer controlled_buffer_2
  assign out_7 = and_6_out ? register_3_q : 8'bz;  // Controlled_Buffer controlled_buffer_3
  assign out_7 = and_8_out ? register_4_q : 8'bz;  // Controlled_Buffer controlled_buffer_4
  assign out_7 = and_10_out ? register_5_q : 8'bz;  // Controlled_Buffer controlled_buffer_5
  assign out_7 = and_12_out ? register_6_q : 8'bz;  // Controlled_Buffer controlled_buffer_6
  assign out_7 = and_14_out ? register_7_q : 8'bz;  // Controlled_Buffer controlled_buffer_7
  assign out_7 = and_16_out ? register_8_q : 8'bz;  // Controlled_Buffer controlled_buffer_8
  assign out_7 = in_6 ? in_3 : 8'bz;  // Controlled_Buffer controlled_buffer_9

  // Notes on the sheet:
  //   read/nwrite
endmodule

module binarydecoder (
  input  lsb,
  input  msb,
  input  en,
  output out_4,
  output out_5,
  output out_6,
  output out_7
);

  and and_1 (out_4, ~lsb, ~msb, en);  // AND_Gate
  and and_2 (out_5, lsb, ~msb, en);  // AND_Gate
  and and_3 (out_6, ~lsb, en, msb);  // AND_Gate
  and and_4 (out_7, lsb, en, msb);
endmodule

module biggerdecoder (
  input  in_1,
  input  in_2,
  input  in_3,
  input  in_4,
  input  in_5
);

  wire binarydecoder_1_out_4, binarydecoder_1_out_5, binarydecoder_1_out_6, binarydecoder_1_out_7,
       binarydecoder_2_out_4, binarydecoder_2_out_5, binarydecoder_2_out_6, binarydecoder_2_out_7,
       binarydecoder_3_out_4, binarydecoder_3_out_5, binarydecoder_3_out_6, binarydecoder_3_out_7,
       binarydecoder_4_out_4, binarydecoder_4_out_5, binarydecoder_4_out_6, binarydecoder_4_out_7,
       binarydecoder_5_out_4, binarydecoder_5_out_5, binarydecoder_5_out_6, binarydecoder_5_out_7;

  binarydecoder binarydecoder_1 (
    .lsb(in_3), .msb(in_4), .en(in_5), .out_4(binarydecoder_1_out_4), .out_5(binarydecoder_1_out_5),
    .out_6(binarydecoder_1_out_6), .out_7(binarydecoder_1_out_7));
  binarydecoder binarydecoder_2 (
    .lsb(in_1), .msb(in_2), .en(binarydecoder_1_out_4), .out_4(binarydecoder_2_out_4),
    .out_5(binarydecoder_2_out_5), .out_6(binarydecoder_2_out_6), .out_7(binarydecoder_2_out_7));
  binarydecoder binarydecoder_3 (
    .lsb(in_1), .msb(in_2), .en(binarydecoder_1_out_5), .out_4(binarydecoder_3_out_4),
    .out_5(binarydecoder_3_out_5), .out_6(binarydecoder_3_out_6), .out_7(binarydecoder_3_out_7));
  binarydecoder binarydecoder_4 (
    .lsb(in_1), .msb(in_2), .en(binarydecoder_1_out_6), .out_4(binarydecoder_4_out_4),
    .out_5(binarydecoder_4_out_5), .out_6(binarydecoder_4_out_6), .out_7(binarydecoder_4_out_7));
  binarydecoder binarydecoder_5 (
    .lsb(in_1), .msb(in_2), .en(binarydecoder_1_out_7), .out_4(binarydecoder_5_out_4),
    .out_5(binarydecoder_5_out_5), .out_6(binarydecoder_5_out_6), .out_7(binarydecoder_5_out_7));
endmodule

module multiplexer (
  input  in_1,
  input  in_2,
  input  in_3,
  output out_4
);

  wire and_1_out, and_2_out;

  and and_1 (and_1_out, in_1, ~in_3);  // AND_Gate
  and and_2 (and_2_out, in_3, in_2);
  or or_1 (out_4, and_1_out, and_2_out);
endmodule

module togleff (
  input  in_1,
  input  in_2,
  input  in_3,
  input  in_4,
  output out_5,
  output out_6
);

  wire multiplexer_1_out;

  Multiplexer #(.enable("false")) multiplexer_1 (.in0(in_1), .in1(out_6), .out(multiplexer_1_out), .sel(in_2));
  D_Flip_Flop d_ff_1 (.clk(in_3), .D(multiplexer_1_out), .Q(out_5), .Qn(out_6), .en(in_4));  // open: preset, reset
endmodule

module counter (
  input  in_1,
  input  in_2,
  input  in_3,
  input  in_4,
  input  in_5,
  input  in_6,
  input  in_7,
  output out_8,
  output out_9,
  output out_10,
  output out_11
);

  wire and_1_out, and_2_out, and_3_out;

  togleff togleff_1 (.in_1(in_4), .in_2(in_1), .in_3(in_2), .in_4(in_3), .out_5(out_8));  // open: out_6
  and and_1 (and_1_out, in_1, out_8);
  togleff togleff_2 (.in_1(in_5), .in_2(and_1_out), .in_3(in_2), .in_4(in_3), .out_5(out_9));  // open: out_6
  and and_2 (and_2_out, and_1_out, out_9);
  togleff togleff_3 (.in_1(in_6), .in_2(and_2_out), .in_3(in_2), .in_4(in_3), .out_5(out_10));  // open: out_6
  and and_3 (and_3_out, and_2_out, out_10);
  togleff togleff_4 (.in_1(in_7), .in_2(and_3_out), .in_3(in_2), .in_4(in_3), .out_5(out_11));  // open: out_6
endmodule
