// Logisim project processor4.circ as structural Verilog: 14 circuits, main circuit fulladder
module fulladder (
  input  a,
  input  b,
  input  c,
  output x,
  output y
);

  wire nand_1_out, nand_2_out, nand_3_out, nand_4_out, nand_5_out, nand_6_out, nand_7_out, nand_8_out,
       nand_9_out, nand_11_out, nand_12_out, nand_13_out, nand_14_out;

  nand nand_1 (nand_1_out, b, c);
  nand nand_2 (nand_2_out, a, c);
  nand nand_3 (nand_3_out, a, b);
  nand nand_4 (nand_4_out, a, a);
  nand nand_5 (nand_5_out, b, b);
  nand nand_6 (nand_6_out, a, a);
  nand nand_7 (nand_7_out, c, c);
  nand nand_8 (nand_8_out, b, b);
  nand nand_9 (nand_9_out, c, c);
  nand nand_10 (x, nand_1_out, nand_2_out, nand_3_out);
  nand nand_11 (nand_11_out, nand_4_out, nand_5_out, c);
  nand nand_12 (nand_12_out, nand_6_out, b, nand_7_out);
  nand nand_13 (nand_13_out, a, nand_8_out, nand_9_out);
  nand nand_14 (nand_14_out, a, b, c);
  nand nand_15 (y, nand_11_out, nand_12_out, nand_13_out, nand_14_out);
endmodule

module add4 (
  input  [3:0] in_1,
  input  [3:0] in_2,
  input  in_3,
  output out_4,
  output [3:0] out_5
);

  wire fulladder_2_x, fulladder_3_x, fulladder_4_x;

  fulladder fulladder_1 (.a(in_1[3]), .b(in_2[3]), .c(fulladder_2_x), .x(out_4), .y(out_5[3]));
  fulladder fulladder_2 (.a(in_1[2]), .b(in_2[2]), .c(fulladder_3_x), .x(fulladder_2_x), .y(out_5[2]));
  fulladder fulladder_3 (.a(in_1[1]), .b(in_2[1]), .c(fulladder_4_x), .x(fulladder_3_x), .y(out_5[1]));
  fulladder fulladder_4 (.a(in_1[0]), .b(in_2[0]), .c(in_3), .x(fulladder_4_x), .y(out_5[0]));
endmodule

module ALU8 (
  input  LSR,
  input  LSL,
  input  XOR,
  input  OR,
  input  AND,
  input  add,
  input  sub,
  input  [7:0] secondbyte,
  input  [7:0] fistbyte,
  output [7:0] out_10,
  output cout,
  output Z,
  output s
);

  wire adder_1_cout, leftshift_1_out_3, or_2_out, rightshift_1_out_2;
  wire [7:0] adder_1_out, and_1_out, bit_extender_1_out, leftshift_1_out_2, or_1_out, rightshift_1_out_3,
       xor_1_out, xor_2_out;

  assign bit_extender_1_out = {{7{sub}}, sub};  // Bit_Extender bit_extender_1
  assign xor_1_out = bit_extender_1_out ^ secondbyte;  // XOR_Gate xor_1, 8 bits wide
  assign and_1_out = secondbyte & fistbyte;  // AND_Gate and_1, 8 bits wide
  assign or_1_out = secondbyte | fistbyte;  // OR_Gate or_1, 8 bits wide
  assign xor_2_out = secondbyte ^ fistbyte;  // XOR_Gate xor_2, 8 bits wide
  leftshift leftshift_1 (.in_1(fistbyte), .out_2(leftshift_1_out_2), .out_3(leftshift_1_out_3));
  rightshift rightshift_1 (.in_1(fistbyte), .out_3(rightshift_1_out_3), .out_2(rightshift_1_out_2));
  Adder adder_1 (.a(xor_1_out), .b(fistbyte), .out(adder_1_out), .cin(sub), .cout(adder_1_cout));
  or or_2 (or_2_out, add, sub);
  assign cout = LSL ? leftshift_1_out_3 : 1'bz;  // Controlled_Buffer controlled_buffer_1
  assign cout = or_2_out ? adder_1_cout : 1'bz;  // Controlled_Buffer controlled_buffer_2
  assign cout = LSR ? rightshift_1_out_2 : 1'bz;  // Controlled_Buffer controlled_buffer_3
  assign out_10 = or_2_out ? adder_1_out : 8'bz;  // Controlled_Buffer controlled_buffer_4
  assign out_10 = AND ? and_1_out : 8'bz;  // Controlled_Buffer controlled_buffer_5
  assign out_10 = OR ? or_1_out : 8'bz;  // Controlled_Buffer controlled_buffer_6
  assign out_10 = XOR ? xor_2_out : 8'bz;  // Controlled_Buffer controlled_buffer_7
  assign out_10 = LSL ? leftshift_1_out_2 : 8'bz;  // Controlled_Buffer controlled_buffer_8
  assign out_10 = LSR ? rightshift_1_out_3 : 8'bz;  // Controlled_Buffer controlled_buffer_9
  nor nor_1 (Z, out_10[0], out_10[1], out_10[2], out_10[3], out_10[5], out_10[6], out_10[7], out_10[4]);

  assign s = out_10[7];

  // Notes on the sheet:
  //   Flag generation circuit
endmodule

module leftshift (
  input  [7:0] in_1,
  output [7:0] out_2,
  output out_3
);


  assign out_2 = {in_1[6:0], 1'b0};
  assign out_3 = in_1[7];
endmodule

module rightshift (
  input  [7:0] in_1,
  output out_2,
  output [7:0] out_3
);


  assign out_2 = in_1[0];
  assign out_3 = {1'b0, in_1[7:1]};
endmodule

module CPU (
);

  wire alu8_1_cout, alu8_1_s, alu8_1_z, and_1_out, and_2_out, and_3_out, and_4_out, and_5_out, and_6_out,
       and_7_out, and_8_out, and_9_out, and_10_out, and_11_out, and_12_out, and_13_out, and_14_out,
       and_15_out, and_16_out, and_17_out, and_18_out, and_19_out, and_20_out, and_21_out, and_22_out,
       and_23_out, and_24_out, and_25_out, and_26_out, and_27_out, and_28_out, and_29_out, and_30_out,
       and_31_out, and_32_out, and_33_out, and_34_out, and_35_out, and_36_out, and_37_out, clock_out,
       clr_2_out, clr_out, controlled_buffer_7_out, d_ff_1_q, d_ff_2_q, d_ff_3_q, decoder_1_out0,
       decoder_1_out1, decoder_1_out2, decoder_1_out3, decoder_1_out4, decoder_1_out5, decoder_1_out6,
       ja_jgt_out, jb_jlt_out, jeq_out, or_1_out, xnor_1_out, xnor_2_out, xnor_3_out, xnor_4_out, xnor_5_out;
  wire [0:0] not_3_out, not_4_out, not_7_out, not_8_out, not_9_out, not_10_out;
  wire [2:0] controlled_buffer_1_out_2, controlled_buffer_1_out_3, controlled_buffer_1_out_4,
       controlled_buffer_1_out_5, Zero_q;
  wire [7:0] alu8_1_out_10, controlled_buffer_37_out, counter_1_q, multiplexer_1_out, multiplexer_2_out,
       multiplexer_3_out, r1_q, r2_q, register_1_q;
  wire [13:0] undriven;
  wire [16:15] xor_1_out;
  wire [20:0] controlled_buffer_1_out, not_1_out, not_2_out;
  wire [20:5] not_5_out, not_6_out;
  wire [20:11] undriven_2, undriven_3, undriven_4;
  wire [20:14] undriven_5, undriven_6, undriven_7;

  Button clr (.out(clr_out));
  D_Flip_Flop d_ff_1 (.clk(clr_out), .D(clock_out), .Q(d_ff_1_q));  // open: Qn, preset, en, reset
  Clock clock (.out(clock_out));
  and and_1 (and_1_out, 1'b1, ~and_37_out);  // AND_Gate
  xnor xnor_1 (xnor_1_out, d_ff_1_q, and_2_out);
  and and_2 (and_2_out, clock_out, and_1_out);
  Register r1 (.D(alu8_1_out_10), .en(controlled_buffer_1_out[0]), .Q(r1_q), .clk(xnor_1_out), .clr(clr_out));
  Register r2 (.D(alu8_1_out_10), .en(controlled_buffer_1_out[1]), .Q(r2_q), .clk(xnor_1_out), .clr(clr_out));
  assign {controlled_buffer_1_out[20], controlled_buffer_1_out_5, controlled_buffer_1_out[16:11], controlled_buffer_1_out_4, controlled_buffer_1_out_3, controlled_buffer_1_out_2, controlled_buffer_1_out[1:0]} = and_3_out ? {7'b1010100, undriven} : 21'bz;  // Controlled_Buffer controlled_buffer_1
  D_Flip_Flop d_ff_2 (
    .clk(xnor_1_out), .D(controlled_buffer_7_out), .Q(d_ff_2_q), .preset(clr_out));  // open: Qn, en, reset
  and and_3 (and_3_out, xnor_1_out, ~d_ff_3_q, ~and_12_out);  // AND_Gate
  and and_4 (and_4_out, and_30_out, d_ff_2_q);
  and and_5 (and_5_out, and_4_out, ~xnor_2_out);  // AND_Gate
  and and_6 (and_6_out, and_31_out, d_ff_2_q);
  and and_7 (and_7_out, and_32_out, d_ff_2_q);
  and and_8 (and_8_out, and_33_out, d_ff_2_q);
  and and_9 (and_9_out, and_8_out, ~xnor_3_out);  // AND_Gate
  and and_10 (and_10_out, and_34_out, d_ff_2_q);
  and and_11 (and_11_out, and_10_out, ~xnor_4_out);  // AND_Gate
  and and_12 (and_12_out, and_35_out, d_ff_2_q);
  and and_13 (and_13_out, and_36_out, d_ff_2_q);
  and and_14 (and_14_out, and_13_out, ~xnor_5_out);  // AND_Gate
  Multiplexer #(.select(3), .width(8), .enable("false")) multiplexer_1 (
    .in0(r1_q), .in1(r2_q), .in2(controlled_buffer_37_out), .in3({8{1'b0}}), .out(multiplexer_1_out),
    .sel(controlled_buffer_1_out_3));  // open: in4, in5, in6, in7
  Multiplexer #(.select(3), .width(8), .enable("false")) multiplexer_2 (
    .in0(r1_q), .in1(r2_q), .in2({8{1'b0}}), .in3(controlled_buffer_37_out), .out(multiplexer_2_out),
    .sel(controlled_buffer_1_out_2));  // open: in4, in5, in6, in7
  not not_1 (not_1_out[0], register_1_q[1]);
  assign {controlled_buffer_1_out[20], controlled_buffer_1_out_5, controlled_buffer_1_out[16:11], controlled_buffer_1_out_4, controlled_buffer_1_out_3, controlled_buffer_1_out_2, controlled_buffer_1_out[1:0]} = and_5_out ? {not_1_out[20:11], 5'b00100, register_1_q[0], 3'b010, register_1_q[1], not_1_out[0]} : 21'bz;  // Controlled_Buffer controlled_buffer_2
  assign {controlled_buffer_1_out[20], controlled_buffer_1_out_5, controlled_buffer_1_out[16:11], controlled_buffer_1_out_4, controlled_buffer_1_out_3, controlled_buffer_1_out_2, controlled_buffer_1_out[1:0]} = and_6_out ? {undriven_2, {11{1'b0}}} : 21'bz;  // Controlled_Buffer controlled_buffer_3
  assign {controlled_buffer_1_out[20], controlled_buffer_1_out_5, controlled_buffer_1_out[16:11], controlled_buffer_1_out_4, controlled_buffer_1_out_3, controlled_buffer_1_out_2, controlled_buffer_1_out[1:0]} = and_7_out ? {undriven_3, {11{1'b0}}} : 21'bz;  // Controlled_Buffer controlled_buffer_4
  not not_2 (not_2_out[0], register_1_q[1]);
  assign {controlled_buffer_1_out[20], controlled_buffer_1_out_5, controlled_buffer_1_out[16:11], controlled_buffer_1_out_4, controlled_buffer_1_out_3, controlled_buffer_1_out_2, controlled_buffer_1_out[1:0]} = and_9_out ? {not_2_out[20:14], 12'he48, register_1_q[1], not_2_out[0]} : 21'bz;  // Controlled_Buffer controlled_buffer_5
  assign {controlled_buffer_1_out[20], controlled_buffer_1_out_5, controlled_buffer_1_out[16:11], controlled_buffer_1_out_4, controlled_buffer_1_out_3, controlled_buffer_1_out_2, controlled_buffer_1_out[1:0]} = and_11_out ? {not_5_out[20:14], 8'he0, not_5_out[5], 2'b00, not_4_out[0], register_1_q[1], not_4_out[0]} : 21'bz;  // Controlled_Buffer controlled_buffer_6
  and jb_jlt (jb_jlt_out, register_1_q[1], ~register_1_q[0]);  // AND_Gate
  assign controlled_buffer_7_out = and_12_out ? 1'b0 : 1'bz;  // Controlled_Buffer controlled_buffer_7
  assign {controlled_buffer_1_out[20], controlled_buffer_1_out_5, controlled_buffer_1_out[16:11], controlled_buffer_1_out_4, controlled_buffer_1_out_3, controlled_buffer_1_out_2, controlled_buffer_1_out[1:0]} = and_12_out ? 21'h150148 : 21'bz;  // Controlled_Buffer controlled_buffer_8
  not not_3 (not_3_out[0], register_1_q[1]);
  assign {controlled_buffer_1_out[20], controlled_buffer_1_out_5, controlled_buffer_1_out[16:11], controlled_buffer_1_out_4, controlled_buffer_1_out_3, controlled_buffer_1_out_2, controlled_buffer_1_out[1:0]} = and_14_out ? {not_6_out[20:14], 8'he0, not_6_out[5], 2'b00, not_3_out[0], 2'b01} : 21'bz;  // Controlled_Buffer controlled_buffer_9
  assign controlled_buffer_7_out = and_5_out ? 1'b1 : 1'bz;  // Controlled_Buffer controlled_buffer_10
  assign controlled_buffer_7_out = and_6_out ? 1'b0 : 1'bz;  // Controlled_Buffer controlled_buffer_11
  assign controlled_buffer_7_out = and_7_out ? 1'b0 : 1'bz;  // Controlled_Buffer controlled_buffer_12
  assign controlled_buffer_7_out = and_9_out ? 1'b1 : 1'bz;  // Controlled_Buffer controlled_buffer_13
  not not_4 (not_4_out[0], register_1_q[1]);
  assign controlled_buffer_7_out = and_11_out ? 1'b1 : 1'bz;  // Controlled_Buffer controlled_buffer_14
  and ja_jgt (ja_jgt_out, ~register_1_q[1], register_1_q[0]);  // AND_Gate
  and and_15 (and_15_out, Zero_q[1], ~Zero_q[0], ja_jgt_out);  // AND_Gate
  and and_16 (and_16_out, Zero_q[2], ~Zero_q[0], Zero_q[1], jb_jlt_out);  // AND_Gate
  or or_1 (or_1_out, and_16_out, and_15_out, and_20_out);
  xor xor_1 (xor_1_out[15], register_1_q[2], or_1_out);
  // Probe on alu8_1_out_10
  xnor xnor_2 (xnor_2_out, register_1_q[0], register_1_q[1]);
  and and_17 (and_17_out, xnor_2_out, and_4_out);
  xnor xnor_3 (xnor_3_out, register_1_q[0], register_1_q[1]);
  and and_18 (and_18_out, and_8_out, xnor_3_out);
  xnor xnor_4 (xnor_4_out, register_1_q[0], register_1_q[1]);
  and and_19 (and_19_out, and_10_out, xnor_4_out);
  not not_5 (not_5_out[5], not_4_out[0]);
  and jeq (jeq_out, ~register_1_q[1], ~register_1_q[0]);  // AND_Gate
  and and_20 (and_20_out, Zero_q[0], jeq_out);
  xnor xnor_5 (xnor_5_out, register_1_q[0], register_1_q[1]);
  and and_21 (and_21_out, and_13_out, xnor_5_out);
  not not_6 (not_6_out[5], not_3_out[0]);
  and and_22 (and_22_out, d_ff_2_q, ~controlled_buffer_7_out);  // AND_Gate
  assign {controlled_buffer_1_out[20], controlled_buffer_1_out_5, controlled_buffer_1_out[16:11], controlled_buffer_1_out_4, controlled_buffer_1_out_3, controlled_buffer_1_out_2, controlled_buffer_1_out[1:0]} = and_17_out ? {undriven_4, {11{1'b0}}} : 21'bz;  // Controlled_Buffer controlled_buffer_15
  assign {controlled_buffer_1_out[20], controlled_buffer_1_out_5, controlled_buffer_1_out[16:11], controlled_buffer_1_out_4, controlled_buffer_1_out_3, controlled_buffer_1_out_2, controlled_buffer_1_out[1:0]} = and_18_out ? {undriven_5, {14{1'b0}}} : 21'bz;  // Controlled_Buffer controlled_buffer_16
  assign {controlled_buffer_1_out[20], controlled_buffer_1_out_5, controlled_buffer_1_out[16:11], controlled_buffer_1_out_4, controlled_buffer_1_out_3, controlled_buffer_1_out_2, controlled_buffer_1_out[1:0]} = and_19_out ? {undriven_6, {14{1'b0}}} : 21'bz;  // Controlled_Buffer controlled_buffer_17
  assign {controlled_buffer_1_out[20], controlled_buffer_1_out_5, controlled_buffer_1_out[16:11], controlled_buffer_1_out_4, controlled_buffer_1_out_3, controlled_buffer_1_out_2, controlled_buffer_1_out[1:0]} = and_21_out ? {undriven_7, {14{1'b0}}} : 21'bz;  // Controlled_Buffer controlled_buffer_18
  Decoder #(.select(3), .enable("false")) decoder_1 (
    .out0(decoder_1_out0), .out1(decoder_1_out1), .out2(decoder_1_out2), .out3(decoder_1_out3),
    .out4(decoder_1_out4), .out5(decoder_1_out5), .out6(decoder_1_out6), .sel(controlled_buffer_1_out_4));  // open: out7
  Counter counter_1 (
    .load(controlled_buffer_1_out[15]), .D(alu8_1_out_10), .count(controlled_buffer_1_out[16]),
    .Q(counter_1_q), .clk(xnor_1_out), .clr(clr_out));  // open: carry
  assign controlled_buffer_7_out = and_17_out ? 1'b0 : 1'bz;  // Controlled_Buffer controlled_buffer_19
  assign controlled_buffer_7_out = and_18_out ? 1'b0 : 1'bz;  // Controlled_Buffer controlled_buffer_20
  assign controlled_buffer_7_out = and_19_out ? 1'b0 : 1'bz;  // Controlled_Buffer controlled_buffer_21
  assign controlled_buffer_7_out = and_21_out ? 1'b0 : 1'bz;  // Controlled_Buffer controlled_buffer_22
  assign controlled_buffer_7_out = and_14_out ? 1'b1 : 1'bz;  // Controlled_Buffer controlled_buffer_23
  ALU8 alu8_1 (
    .LSR(decoder_1_out6), .LSL(decoder_1_out5), .XOR(decoder_1_out4), .OR(decoder_1_out3),
    .AND(decoder_1_out2), .add(decoder_1_out1), .secondbyte(multiplexer_2_out), .fistbyte(multiplexer_1_out),
    .out_10(alu8_1_out_10), .cout(alu8_1_cout), .sub(decoder_1_out0), .Z(alu8_1_z), .s(alu8_1_s));
  D_Flip_Flop d_ff_3 (.clk(xnor_1_out), .D(and_22_out), .Q(d_ff_3_q), .reset(clr_out));  // open: Qn, preset, en
  D_Flip_Flop Zero (
    .clk(xnor_1_out), .D(alu8_1_z), .Q(Zero_q[0]), .en(controlled_buffer_1_out[13]), .reset(clr_out));  // open: Qn, preset
  and and_23 (and_23_out, and_30_out, d_ff_3_q);
  and and_24 (and_24_out, and_31_out, d_ff_3_q);
  and and_25 (and_25_out, and_32_out, d_ff_3_q);
  and and_26 (and_26_out, and_33_out, d_ff_3_q);
  assign {controlled_buffer_1_out[20], controlled_buffer_1_out_5, controlled_buffer_1_out[16:11], controlled_buffer_1_out_4, controlled_buffer_1_out_3, controlled_buffer_1_out_2, controlled_buffer_1_out[1:0]} = and_26_out ? {18'h2a728, {2{register_1_q[1]}}, not_8_out[0]} : 21'bz;  // Controlled_Buffer controlled_buffer_24
  and and_27 (and_27_out, and_34_out, d_ff_3_q);
  assign {controlled_buffer_1_out[20], controlled_buffer_1_out_5, controlled_buffer_1_out[16:11], controlled_buffer_1_out_4, controlled_buffer_1_out_3, controlled_buffer_1_out_2, controlled_buffer_1_out[1:0]} = and_27_out ? {15'h54e0, register_1_q[1], 3'b011, register_1_q[1], not_9_out[0]} : 21'bz;  // Controlled_Buffer controlled_buffer_25
  and and_28 (and_28_out, and_35_out, d_ff_3_q);
  assign controlled_buffer_7_out = and_28_out ? 1'b1 : 1'bz;  // Controlled_Buffer controlled_buffer_26
  and and_29 (and_29_out, and_36_out, d_ff_3_q);
  D_Flip_Flop Carry (
    .clk(xnor_1_out), .D(alu8_1_cout), .Q(Zero_q[1]), .en(controlled_buffer_1_out[12]), .reset(clr_out));  // open: Qn, preset
  Multiplexer #(.select(3), .width(8), .enable("false")) multiplexer_3 (
    .in0(r1_q), .in1(r2_q), .in2(counter_1_q), .out(multiplexer_3_out), .sel(controlled_buffer_1_out_5));  // open: in3, in4, in5, in6, in7
  not not_7 (not_7_out[0], register_1_q[0]);
  assign {controlled_buffer_1_out[20], controlled_buffer_1_out_5, controlled_buffer_1_out[16:11], controlled_buffer_1_out_4, controlled_buffer_1_out_3, controlled_buffer_1_out_2, controlled_buffer_1_out[1:0]} = and_23_out ? {19'h54052, register_1_q[0], not_7_out[0]} : 21'bz;  // Controlled_Buffer controlled_buffer_27
  assign controlled_buffer_7_out = and_23_out ? 1'b1 : 1'bz;  // Controlled_Buffer controlled_buffer_28
  assign controlled_buffer_7_out = and_24_out ? 1'b1 : 1'bz;  // Controlled_Buffer controlled_buffer_29
  assign {controlled_buffer_1_out[20], controlled_buffer_1_out_5, controlled_buffer_1_out[16:11], controlled_buffer_1_out_4, controlled_buffer_1_out_3, controlled_buffer_1_out_2, controlled_buffer_1_out[1:0]} = and_24_out ? {3'b100, register_1_q[0], 15'h52, register_1_q[1], not_10_out[0]} : 21'bz;  // Controlled_Buffer controlled_buffer_30
  assign {controlled_buffer_1_out[20], controlled_buffer_1_out_5, controlled_buffer_1_out[16:11], controlled_buffer_1_out_4, controlled_buffer_1_out_3, controlled_buffer_1_out_2, controlled_buffer_1_out[1:0]} = and_25_out ? {3'b000, register_1_q[1], 11'h104, register_1_q[0], 5'b01000} : 21'bz;  // Controlled_Buffer controlled_buffer_31
  assign controlled_buffer_7_out = and_25_out ? 1'b1 : 1'bz;  // Controlled_Buffer controlled_buffer_32
  not not_8 (not_8_out[0], register_1_q[1]);
  assign controlled_buffer_7_out = and_26_out ? 1'b1 : 1'bz;  // Controlled_Buffer controlled_buffer_33
  not not_9 (not_9_out[0], register_1_q[1]);
  assign controlled_buffer_7_out = and_27_out ? 1'b1 : 1'bz;  // Controlled_Buffer controlled_buffer_34
  assign {controlled_buffer_1_out[20], controlled_buffer_1_out_5, controlled_buffer_1_out[16:11], controlled_buffer_1_out_4, controlled_buffer_1_out_3, controlled_buffer_1_out_2, controlled_buffer_1_out[1:0]} = and_28_out ? {4'b1010, xor_1_out, 15'h148} : 21'bz;  // Controlled_Buffer controlled_buffer_35
  assign {controlled_buffer_1_out[20], controlled_buffer_1_out_5, controlled_buffer_1_out[16:11], controlled_buffer_1_out_4, controlled_buffer_1_out_3, controlled_buffer_1_out_2, controlled_buffer_1_out[1:0]} = and_29_out ? {15'h54e0, register_1_q[1], 5'b01100} : 21'bz;  // Controlled_Buffer controlled_buffer_36
  D_Flip_Flop sign (
    .clk(xnor_1_out), .D(alu8_1_s), .Q(Zero_q[2]), .en(controlled_buffer_1_out[11]), .reset(clr_out));  // open: Qn, preset
  assign controlled_buffer_37_out = controlled_buffer_1_out[14] ? alu8_1_out_10 : 8'bz;  // Controlled_Buffer controlled_buffer_37
  not not_10 (not_10_out[0], register_1_q[1]);
  not not_11 (xor_1_out[16], xor_1_out[15]);
  assign controlled_buffer_7_out = and_29_out ? 1'b1 : 1'bz;  // Controlled_Buffer controlled_buffer_38
  Button clr_2 (.out(clr_2_out));
  RAM_part ram_1 (
    .addr(multiplexer_3_out), .data(controlled_buffer_37_out), .sel(1'b1), .clk(xnor_1_out),
    .ld(controlled_buffer_1_out[20]), .clr(clr_2_out));
  // Probe on Zero_q
  Register #(.trigger("falling")) register_1 (
    .D(controlled_buffer_37_out), .en(d_ff_2_q), .Q(register_1_q), .clk(xnor_1_out), .clr(clr_out));
  and and_30 (and_30_out, ~register_1_q[2], ~register_1_q[3], ~register_1_q[4], ~register_1_q[6], ~register_1_q[7], ~register_1_q[5]);  // AND_Gate
  and and_31 (and_31_out, register_1_q[2], ~register_1_q[3], ~register_1_q[4], ~register_1_q[6], ~register_1_q[7], ~register_1_q[5]);  // AND_Gate
  and and_32 (and_32_out, ~register_1_q[2], register_1_q[3], ~register_1_q[4], ~register_1_q[6], ~register_1_q[7], ~register_1_q[5]);  // AND_Gate
  and and_33 (and_33_out, ~register_1_q[2], ~register_1_q[3], register_1_q[4], ~register_1_q[6], ~register_1_q[7], ~register_1_q[5]);  // AND_Gate
  and and_34 (and_34_out, ~register_1_q[2], ~register_1_q[3], ~register_1_q[4], register_1_q[5], ~register_1_q[6], ~register_1_q[7]);  // AND_Gate
  and and_35 (and_35_out, ~register_1_q[3], register_1_q[4], register_1_q[5], register_1_q[6], register_1_q[7]);  // AND_Gate
  and and_36 (and_36_out, register_1_q[3], register_1_q[4], register_1_q[5], register_1_q[6], register_1_q[7]);
  and and_37 (and_37_out, register_1_q[0], register_1_q[1], register_1_q[2], register_1_q[3], register_1_q[5], register_1_q[6], register_1_q[7], register_1_q[4]);

  // Notes on the sheet:
  //   Move
  //   Load
  //   A
  //   B
  //   Store
  //   Add
  //   Sub
  //   Jump
  //   cmp
  //   Sel-y
  //   Sel-x
  //   F-bus
  //   instruction pointer
  //   MOV r,[r]
  //   str r,[r]
  //   Add r,r
  //   sub r,r
  //   opperation
  //   register and immediate value to the register
  //   IP
  //   A-bus
  //   ALU-o/p
  //   RAM
  //   D-bus
endmodule

module latch1 (
  input  D,
  input  en,
  input  in_3,
  output Q
);

  wire and_1_out, and_2_out, nor_1_out, not_1_out, or_1_out;

  not not_1 (not_1_out, D);
  and and_1 (and_1_out, D, en);
  and and_2 (and_2_out, en, not_1_out);
  or or_1 (or_1_out, and_2_out, in_3);
  nor nor_1 (nor_1_out, and_1_out, Q);
  nor nor_2 (Q, nor_1_out, or_1_out);
endmodule

module msDff (
  input  data,
  input  clk,
  input  reset,
  output out_4
);

  wire latch1_1_q, not_1_out;

  latch1 latch1_1 (.D(data), .en(clk), .Q(latch1_1_q), .in_3(reset));
  not not_1 (not_1_out, clk);
  latch1 latch1_2 (.D(latch1_1_q), .en(not_1_out), .Q(out_4), .in_3(reset));
endmodule

module RAM (
  input  in_1,
  input  [2:0] in_2,
  input  [7:0] in_3,
  input  in_4,
  input  in_5,
  input  in_6,
  output [7:0] out_7
);

  wire and_1_out, and_2_out, and_3_out, and_4_out, and_5_out, and_6_out, and_7_out, and_8_out, and_9_out,
       and_10_out, and_11_out, and_12_out, and_13_out, and_14_out, and_15_out, and_16_out, decoder_1_out0,
       decoder_1_out1, decoder_1_out2, decoder_1_out3, decoder_1_out4, decoder_1_out5, decoder_1_out6,
       decoder_1_out7;
  wire [7:0] register_1_q, register_2_q, register_3_q, register_4_q, register_5_q, register_6_q,
       register_7_q, register_8_q;

  Decoder #(.select(3)) decoder_1 (
    .out0(decoder_1_out0), .out1(decoder_1_out1), .out2(decoder_1_out2), .out3(decoder_1_out3),
    .out4(decoder_1_out4), .out5(decoder_1_out5), .out6(decoder_1_out6), .out7(decoder_1_out7), .sel(in_2),
    .en(in_1));
  and and_1 (and_1_out, ~in_4, decoder_1_out0);  // AND_Gate
  and and_2 (and_2_out, decoder_1_out0, in_4);
  and and_3 (and_3_out, ~in_4, decoder_1_out1);  // AND_Gate
  and and_4 (and_4_out, decoder_1_out1, in_4);
  and and_5 (and_5_out, ~in_4, decoder_1_out2);  // AND_Gate
  and and_6 (and_6_out, decoder_1_out2, in_4);
  and and_7 (and_7_out, ~in_4, decoder_1_out3);  // AND_Gate
  and and_8 (and_8_out, decoder_1_out3, in_4);
  and and_9 (and_9_out, ~in_4, decoder_1_out4);  // AND_Gate
  and and_10 (and_10_out, decoder_1_out4, in_4);
  and and_11 (and_11_out, ~in_4, decoder_1_out5);  // AND_Gate
  and and_12 (and_12_out, decoder_1_out5, in_4);
  and and_13 (and_13_out, ~in_4, decoder_1_out6);  // AND_Gate
  and and_14 (and_14_out, decoder_1_out6, in_4);
  and and_15 (and_15_out, ~in_4, decoder_1_out7);  // AND_Gate
  and and_16 (and_16_out, decoder_1_out7, in_4);
  Register register_1 (.D(out_7), .en(and_1_out), .Q(register_1_q), .clk(in_5));  // open: clr
  Register register_2 (.D(out_7), .en(and_3_out), .Q(register_2_q), .clk(in_5));  // open: clr
  Register register_3 (.D(out_7), .en(and_5_out), .Q(register_3_q), .clk(in_5));  // open: clr
  Register register_4 (.D(out_7), .en(and_7_out), .Q(register_4_q), .clk(in_5));  // open: clr
  Register register_5 (.D(out_7), .en(and_9_out), .Q(register_5_q), .clk(in_5));  // open: clr
  Register register_6 (.D(out_7), .en(and_11_out), .Q(register_6_q), .clk(in_5));  // open: clr
  Register register_7 (.D(out_7), .en(and_13_out), .Q(register_7_q), .clk(in_5));  // open: clr
  Register register_8 (.D(out_7), .en(and_15_out), .Q(register_8_q), .clk(in_5));  // open: clr
  assign out_7 = and_2_out ? register_1_q : 8'bz;  // Controlled_Buffer controlled_buffer_1
  assign out_7 = and_4_out ? register_2_q : 8'bz;  // Controlled_Buffer controlled_buffer_2
  assign out_7 = and_6_out ? register_3_q : 8'bz;  // Controlled_Buffer controlled_buffer_3
  assign out_7 = and_8_out ? register_4_q : 8'bz;  // Controlled_Buffer controlled_buffer_4
  assign out_7 = and_10_out ? register_5_q : 8'bz;  // Controlled_Buffer controlled_buffer_5
  assign out_7 = and_12_out ? register_6_q : 8'bz;  // Controlled_Buffer controlled_buffer_6
  assign out_7 = and_14_out ? register_7_q : 8'bz;  // Controlled_Buffer controlled_buffer_7
  assign out_7 = and_16_out ? register_8_q : 8'bz;  // Controlled_Buffer controlled_buffer_8
  assign out_7 = in_6 ? in_3 : 8'bz;  // Controlled_Buffer controlled_buffer_9

  // Notes on the sheet:
  //   read/nwrite
endmodule

module binarydecoder (
  input  lsb,
  input  msb,
  input  en,
  output out_4,
  output out_5,
  output out_6,
  output out_7
);

  and and_1 (out_4, ~lsb, ~msb, en);  // AND_Gate
  and and_2 (out_5, lsb, ~msb, en);  // AND_Gate
  and and_3 (out_6, ~lsb, en, msb);  // AND_Gate
  and and_4 (out_7, lsb, en, msb);
endmodule

module biggerdecoder (
  input  in_1,
  input  in_2,
  input  in_3,
  input  in_4,
  input  in_5
);

  wire binarydecoder_1_out_4, binarydecoder_1_out_5, binarydecoder_1_out_6, binarydecoder_1_out_7,
       binarydecoder_2_out_4, binarydecoder_2_out_5, binarydecoder_2_out_6, binarydecoder_2_out_7,
       binarydecoder_3_out_4, binarydecoder_3_out_5, binarydecoder_3_out_6, binarydecoder_3_out_7,
       binarydecoder_4_out_4, binarydecoder_4_out_5, binarydecoder_4_out_6, binarydecoder_4_out_7,
       binarydecoder_5_out_4, binarydecoder_5_out_5, binarydecoder_5_out_6, binarydecoder_5_out_7;

  binarydecoder binarydecoder_1 (
    .lsb(in_3), .msb(in_4), .en(in_5), .out_4(binarydecoder_1_out_4), .out_5(binarydecoder_1_out_5),
    .out_6(binarydecoder_1_out_6), .out_7(binarydecoder_1_out_7));
  binarydecoder binarydecoder_2 (
    .lsb(in_1), .msb(in_2), .en(binarydecoder_1_out_4), .out_4(binarydecoder_2_out_4),
    .out_5(binarydecoder_2_out_5), .out_6(binarydecoder_2_out_6), .out_7(binarydecoder_2_out_7));
  binarydecoder binarydecoder_3 (
    .lsb(in_1), .msb(in_2), .en(binarydecoder_1_out_5), .out_4(binarydecoder_3_out_4),
    .out_5(binarydecoder_3_out_5), .out_6(binarydecoder_3_out_6), .out_7(binarydecoder_3_out_7));
  binarydecoder binarydecoder_4 (
    .lsb(in_1), .msb(in_2), .en(binarydecoder_1_out_6), .out_4(binarydecoder_4_out_4),
    .out_5(binarydecoder_4_out_5), .out_6(binarydecoder_4_out_6), .out_7(binarydecoder_4_out_7));
  binarydecoder binarydecoder_5 (
    .lsb(in_1), .msb(in_2), .en(binarydecoder_1_out_7), .out_4(binarydecoder_5_out_4),
    .out_5(binarydecoder_5_out_5), .out_6(binarydecoder_5_out_6), .out_7(binarydecoder_5_out_7));
endmodule

module multiplexer (
  input  in_1,
  input  in_2,
  input  in_3,
  output out_4
);

  wire and_1_out, and_2_out;

  and and_1 (and_1_out, in_1, ~in_3);  // AND_Gate
  and and_2 (and_2_out, in_3, in_2);
  or or_1 (out_4, and_1_out, and_2_out);
endmodule

module togleff (
  input  in_1,
  input  in_2,
  input  in_3,
  input  in_4,
  output out_5,
  output out_6
);

  wire multiplexer_1_out;

  Multiplexer #(.enable("false")) multiplexer_1 (.in0(in_1), .in1(out_6), .out(multiplexer_1_out), .sel(in_2));
  D_Flip_Flop d_ff_1 (.clk(in_3), .D(multiplexer_1_out), .Q(out_5), .Qn(out_6), .en(in_4));  // open: preset, reset
endmodule

module counter (
  input  in_1,
  input  in_2,
  input  in_3,
  input  in_4,
  input  in_5,
  input  in_6,
  input  in_7,
  output out_8,
  output out_9,
  output out_10,
  output out_11
);

  wire and_1_out, and_2_out, and_3_out;

  togleff togleff_1 (.in_1(in_4), .in_2(in_1), .in_3(in_2), .in_4(in_3), .out_5(out_8));  // open: out_6
  and and_1 (and_1_out, in_1, out_8);
  togleff togleff_2 (.in_1(in_5), .in_2(and_1_out), .in_3(in_2), .in_4(in_3), .out_5(out_9));  // open: out_6
  and and_2 (and_2_out, and_1_out, out_9);
  togleff togleff_3 (.in_1(in_6), .in_2(and_2_out), .in_3(in_2), .in_4(in_3), .out_5(out_10));  // open: out_6
  and and_3 (and_3_out, and_2_out, out_10);
  togleff togleff_4 (.in_1(in_7), .in_2(and_3_out), .in_3(in_2), .in_4(in_3), .out_5(out_11));  // open: out_6
endmodule
